// Logisim project CPU-8-BITS.circ as structural Verilog: 14 circuits, main circuit main
// 8 BIT CPU
module CPU (
  input  clock,
  input  bt_reset,
  input  run,
  input  [7:0] data,
  output hlt,
  output aci,
  output [7:0] a_reg,
  output pci,
  output sub,
  output [7:0] b_reg,
  output jmp,
  output al1,
  output [7:0] \output ,
  output pco,
  output al0,
  output mai,
  output alu,
  output [7:0] bus,
  output iri,
  output \not ,
  output [7:0] alu_out,
  output iro,
  output bri,
  output [7:0] ir_out,
  output aco,
  output ori,
  output [3:0] address,
  output [4:0] counter,
  output rmi,
  output rmo,
  output overflow
);

  wire ACI_t, ACO_t, ALU_t, BRI_t, CLOCK_t, control_1_aci, control_1_aco, control_1_alu, control_1_bri,
       control_1_iri, control_1_iro, control_1_jmp, control_1_mai, control_1_ori, control_1_pco, IRI_t,
       IRO_t, JMP_t, MAI_t, nCLOCK, nCYCLE_END, nCYCLE_RST, nRESET, ORI_t, PCO_t, RESET;
  wire [2:0] counter_1_couter_out;
  wire [3:0] ir_1_control;

  not not_1 (JMP_t, control_1_jmp);
  not not_2 (PCO_t, control_1_pco);
  not not_3 (MAI_t, control_1_mai);
  not not_4 (IRI_t, control_1_iri);
  not not_5 (IRO_t, control_1_iro);
  Multiplexer #(.enable("false")) multiplexer_1 (.in0(clock), .in1(1'b0), .out(CLOCK_t), .sel(hlt));
  not not_6 (nCLOCK, CLOCK_t);
  CONTROL control_1 (
    .HLT(hlt), .PCI(pci), .JMP(control_1_jmp), .PCO(control_1_pco), .MAI(control_1_mai), .RMI(rmi),
    .RMO(rmo), .IRI(control_1_iri), .IRO(control_1_iro), .ACO(control_1_aco), .ACI(control_1_aci), .SUB(sub),
    .AL1(al1), .AL0(al0), .ALU(control_1_alu), .NOT(\not ), .BRI(control_1_bri), .ORI(control_1_ori),
    .i3(ir_1_control[3]), .i2(ir_1_control[2]), .i1(ir_1_control[1]), .i0(ir_1_control[0]),
    .c2(counter_1_couter_out[2]), .c1(counter_1_couter_out[1]), .c0(counter_1_couter_out[0]));
  COUNTER counter_1 (
    .nclock(nCLOCK), .ncycle_rst(nCYCLE_RST), .ncycle_end(nCYCLE_END), .status(counter),
    .couter_out(counter_1_couter_out));
  PC pc_1 (
    .pc_inc(pci), .pc_out(PCO_t), .reset(RESET), .jmp(JMP_t), .BUS_OUT(data), .clock(CLOCK_t), .BUS_IN(data));  // open: in_7
  MAR mar_1 (.clock(CLOCK_t), .mar_in(MAI_t), .run(run), .reset(RESET), .BUS_IN(data), .ram(address));  // open: dips
  IR ir_1 (
    .clock(CLOCK_t), .ir_in(IRI_t), .ir_out(IRO_t), .reset(RESET), .BUS_OUT(data), .BUS_IN(data),
    .control(ir_1_control), .signal_out(ir_out));  // open: in_5
  RESET reset_1 (.bt_reset(bt_reset), .ncycle_end(nCYCLE_END), .nreset(nRESET), .reset(RESET), .ncycle_rst(nCYCLE_RST));
  not not_7 (ACO_t, control_1_aco);
  not not_8 (ACI_t, control_1_aci);
  not not_9 (ALU_t, control_1_alu);
  not not_10 (BRI_t, control_1_bri);
  not not_11 (ORI_t, control_1_ori);
  not not_12 (jmp, JMP_t);
  not not_13 (pco, PCO_t);
  not not_14 (mai, MAI_t);
  not not_15 (iri, IRI_t);
  not not_16 (iro, IRO_t);
  not not_17 (aco, ACO_t);
  ACC_REGISTER acc_register_1 (
    .clock(CLOCK_t), .acc_in(ACI_t), .acc_out(ACO_t), .reset(RESET), .BUS_OUT(data), .BUS_IN(data),
    .signal_out(a_reg));  // open: in_5
  ALU alu_1 (
    .alu_out(ALU_t), .bus_out(data), .add_sub(sub), .a_in(a_reg), .b_in(b_reg), .xor_not(\not ),
    .signal_out(alu_out), .alu_0(al0), .alu_1(al1), .overflow(overflow));  // open: in_8
  B_REGISTER B_REGISTER (.clock(CLOCK_t), .br_in(BRI_t), .reset(RESET), .BUS_IN(data), .signal_out(b_reg));
  OR or_1 (.clock(CLOCK_t), .bus_in(data), .opr_in(ORI_t), .signal_out(\output ), .reset(RESET));
  not not_18 (aci, ACI_t);
  not not_19 (alu, ALU_t);
  not not_20 (bri, BRI_t);
  not not_21 (ori, ORI_t);

  assign bus = data;

  // Other names for the same wires on the sheet: SIGNAL_ALU[7:0] = alu_out
endmodule

module main (
  input  run,
  input  signal
);

  wire ACI, ACO, AL_0, AL_1, ALU, BRI, CLOCK, HLT, IRI, IRO, JMP, MAI, multiplexer_1_out, NOT, ORI, OVERFLOW,
       PCI, PCO, RESET, RMI, RMO, SUB;
  wire [3:0] ADDRESS;
  wire [4:0] COUNTER;
  wire [6:0] display_1_hunds, display_1_tens, display_1_units;
  wire [7:0] A_REG, ALU_OUT, B_REG, BUS, DATA, IR_OUT, OUTPUT;

  Clock clock_1 (.out(CLOCK));
  Button button_1 (.out(RESET));
  LED led_1 (.in(HLT));
  LED led_2 (.in(ORI));
  LED led_3 (.in(PCI));
  LED led_4 (.in(ACI));
  CPU cpu_1 (
    .clock(CLOCK), .hlt(HLT), .aci(ACI), .a_reg(A_REG), .pci(PCI), .sub(SUB), .b_reg(B_REG), .jmp(JMP),
    .al1(AL_1), .\output (OUTPUT), .pco(PCO), .al0(AL_0), .mai(MAI), .alu(ALU), .bus(BUS), .iri(IRI),
    .\not (NOT), .alu_out(ALU_OUT), .iro(IRO), .bri(BRI), .bt_reset(RESET), .ir_out(IR_OUT), .aco(ACO),
    .ori(ORI), .address(ADDRESS), .counter(COUNTER), .run(run), .rmi(RMI), .data(DATA), .rmo(RMO),
    .overflow(OVERFLOW));
  LED led_5 (.in(SUB));
  LED led_6 (.in(AL_1));
  LED led_7 (.in(JMP));
  LED led_8 (.in(AL_0));
  LED led_9 (.in(PCO));
  RAM #(.addrWidth(4), .bus("separate")) ram_1 (
    .addr(ADDRESS), .din(BUS), .data(DATA), .str(RMI), .sel(1'b1), .clk(CLOCK), .ld(RMO), .clr(1'b0));
  LED led_10 (.in(MAI));
  LED led_11 (.in(OUTPUT[6]));
  LED led_12 (.in(OUTPUT[7]));
  LED led_13 (.in(DATA[6]));
  LED led_14 (.in(DATA[7]));
  LED led_15 (.in(A_REG[6]));
  LED led_16 (.in(A_REG[7]));
  LED led_17 (.in(COUNTER[0]));
  LED led_18 (.in(COUNTER[1]));
  LED led_19 (.in(ALU));
  LED led_20 (.in(IRI));
  LED led_21 (.in(OUTPUT[4]));
  LED led_22 (.in(OUTPUT[3]));
  LED led_23 (.in(OUTPUT[5]));
  LED led_24 (.in(DATA[5]));
  LED led_25 (.in(DATA[4]));
  LED led_26 (.in(DATA[3]));
  LED led_27 (.in(A_REG[4]));
  LED led_28 (.in(A_REG[5]));
  LED led_29 (.in(COUNTER[2]));
  LED led_30 (.in(COUNTER[3]));
  LED led_31 (.in(NOT));
  LED led_32 (.in(OUTPUT[2]));
  LED led_33 (.in(OUTPUT[0]));
  LED led_34 (.in(OUTPUT[1]));
  LED led_35 (.in(DATA[0]));
  LED led_36 (.in(DATA[1]));
  LED led_37 (.in(DATA[2]));
  LED led_38 (.in(A_REG[1]));
  LED led_39 (.in(A_REG[2]));
  LED led_40 (.in(A_REG[3]));
  LED led_41 (.in(COUNTER[4]));
  LED led_42 (.in(IRO));
  LED led_43 (.in(BRI));
  _7_Segment_Display u_7_segment_display_1 (
    .g(multiplexer_1_out), .f(1'b0), .a(1'b0), .b(1'b0), .e(1'b0), .d(1'b0), .c(1'b0), .dp(1'b0));
  LED led_44 (.in(A_REG[0]));
  LED led_45 (.in(ADDRESS[2]));
  LED led_46 (.in(ADDRESS[3]));
  LED led_47 (.in(ACO));
  LED led_48 (.in(B_REG[6]));
  LED led_49 (.in(B_REG[7]));
  LED led_50 (.in(ADDRESS[0]));
  LED led_51 (.in(ADDRESS[1]));
  LED led_52 (.in(OVERFLOW));
  Multiplexer #(.enable("false")) multiplexer_1 (.in0(1'b0), .in1(OUTPUT[7]), .out(multiplexer_1_out), .sel(signal));
  LED led_53 (.in(B_REG[3]));
  LED led_54 (.in(B_REG[4]));
  LED led_55 (.in(B_REG[5]));
  LED led_56 (.in(IR_OUT[7]));
  LED led_57 (.in(IR_OUT[6]));
  LED led_58 (.in(BUS[7]));
  _7_Segment_Display u_7_segment_display_2 (
    .g(display_1_hunds[5]), .f(display_1_hunds[6]), .a(display_1_hunds[4]), .b(display_1_hunds[3]),
    .e(display_1_hunds[0]), .d(display_1_hunds[1]), .c(display_1_hunds[2]));  // open: dp
  LED led_59 (.in(B_REG[2]));
  LED led_60 (.in(B_REG[0]));
  LED led_61 (.in(B_REG[1]));
  LED led_62 (.in(IR_OUT[4]));
  LED led_63 (.in(IR_OUT[5]));
  LED led_64 (.in(BUS[5]));
  LED led_65 (.in(BUS[4]));
  LED led_66 (.in(BUS[6]));
  DISPLAY display_1 (
    .signal(multiplexer_1_out), .LT(1'b1), .BL(1'b1), .LE(1'b1), .\input (OUTPUT), .units(display_1_units),
    .hunds(display_1_hunds), .tens(display_1_tens));
  LED led_67 (.in(IR_OUT[1]));
  LED led_68 (.in(IR_OUT[3]));
  LED led_69 (.in(IR_OUT[2]));
  LED led_70 (.in(BUS[2]));
  LED led_71 (.in(BUS[1]));
  LED led_72 (.in(BUS[3]));
  _7_Segment_Display u_7_segment_display_3 (
    .g(display_1_tens[5]), .f(display_1_tens[6]), .a(display_1_tens[4]), .b(display_1_tens[3]),
    .e(display_1_tens[0]), .d(display_1_tens[1]), .c(display_1_tens[2]));  // open: dp
  LED led_73 (.in(ALU_OUT[7]));
  LED led_74 (.in(ALU_OUT[6]));
  LED led_75 (.in(ALU_OUT[5]));
  LED led_76 (.in(IR_OUT[0]));
  LED led_77 (.in(BUS[0]));
  LED led_78 (.in(ALU_OUT[2]));
  LED led_79 (.in(ALU_OUT[3]));
  LED led_80 (.in(ALU_OUT[4]));
  _7_Segment_Display u_7_segment_display_4 (
    .g(display_1_units[5]), .f(display_1_units[6]), .a(display_1_units[4]), .b(display_1_units[3]),
    .e(display_1_units[0]), .d(display_1_units[1]), .c(display_1_units[2]));  // open: dp
  LED led_81 (.in(ALU_OUT[0]));
  LED led_82 (.in(ALU_OUT[1]));

  // Other names for the same wires on the sheet: SIGNAL_OUT = OUTPUT[7]
endmodule

module PC (
  input  clock,
  input  pc_inc,
  input  pc_out,
  input  reset,
  input  jmp,
  input  [7:0] BUS_IN,
  input  [7:0] in_7,
  output [7:0] BUS_OUT
);

  wire [3:0] adder_1_out, multiplexer_1_out, multiplexer_2_out, register_1_q;

  Multiplexer #(.width(4), .enable("false")) multiplexer_1 (
    .in0(BUS_IN[3:0]), .in1(adder_1_out), .out(multiplexer_1_out), .sel(jmp));
  Register #(.width(4)) register_1 (.D(multiplexer_1_out), .en(1'b1), .Q(register_1_q), .clk(clock), .clr(reset));
  Multiplexer #(.width(4), .enable("false")) multiplexer_2 (
    .in0(4'b0000), .in1(4'b0001), .out(multiplexer_2_out), .sel(pc_inc));
  LED led_1 (.in(register_1_q[2]));
  LED led_2 (.in(register_1_q[3]));
  Adder #(.width(4)) adder_1 (.a(register_1_q), .b(multiplexer_2_out), .out(adder_1_out));  // open: cin, cout
  LED led_3 (.in(register_1_q[0]));
  LED led_4 (.in(register_1_q[1]));
  Multiplexer #(.width(8), .enable("false")) multiplexer_3 (
    .in0({4'b0000, register_1_q}), .in1(in_7), .out(BUS_OUT), .sel(pc_out));
endmodule

module ACC_REGISTER (
  input  clock,
  input  acc_in,
  input  acc_out,
  input  reset,
  input  [7:0] in_5,
  input  [7:0] BUS_IN,
  output [7:0] BUS_OUT,
  output [7:0] signal_out
);

  wire [7:0] multiplexer_1_out;

  Multiplexer #(.width(8), .enable("false")) multiplexer_1 (
    .in0(BUS_IN), .in1(signal_out), .out(multiplexer_1_out), .sel(acc_in));
  LED led_1 (.in(signal_out[6]));
  LED led_2 (.in(signal_out[7]));
  LED led_3 (.in(signal_out[5]));
  LED led_4 (.in(signal_out[4]));
  LED led_5 (.in(signal_out[3]));
  Register register_1 (.D(multiplexer_1_out), .Q(signal_out), .clk(clock), .clr(reset));  // open: en
  LED led_6 (.in(signal_out[2]));
  LED led_7 (.in(signal_out[0]));
  LED led_8 (.in(signal_out[1]));
  Multiplexer #(.width(8), .enable("false")) multiplexer_2 (.in0(signal_out), .in1(in_5), .out(BUS_OUT), .sel(acc_out));
endmodule

module B_REGISTER (
  input  clock,
  input  br_in,
  input  reset,
  input  [7:0] BUS_IN,
  output [7:0] signal_out
);

  wire [7:0] multiplexer_1_out;

  Multiplexer #(.width(8), .enable("false")) multiplexer_1 (
    .in0(BUS_IN), .in1(signal_out), .out(multiplexer_1_out), .sel(br_in));
  LED led_1 (.in(signal_out[6]));
  LED led_2 (.in(signal_out[7]));
  LED led_3 (.in(signal_out[5]));
  LED led_4 (.in(signal_out[4]));
  LED led_5 (.in(signal_out[3]));
  Register register_1 (.D(multiplexer_1_out), .Q(signal_out), .clk(clock), .clr(reset));  // open: en
  LED led_6 (.in(signal_out[0]));
  LED led_7 (.in(signal_out[2]));
  LED led_8 (.in(signal_out[1]));
endmodule

module IR (
  input  clock,
  input  ir_in,
  input  ir_out,
  input  reset,
  input  [7:0] in_5,
  input  [7:0] BUS_IN,
  output [7:0] signal_out,
  output [7:0] BUS_OUT,
  output [3:0] control
);

  wire [7:0] multiplexer_1_out;

  Multiplexer #(.width(8), .enable("false")) multiplexer_1 (
    .in0(BUS_IN), .in1({control, signal_out[3:0]}), .out(multiplexer_1_out), .sel(ir_in));
  LED led_1 (.in(control[2]));
  LED led_2 (.in(control[3]));
  LED led_3 (.in(control[1]));
  // Probe on control
  LED led_4 (.in(control[0]));
  LED led_5 (.in(signal_out[3]));
  Register register_1 (.D(multiplexer_1_out), .Q({control, signal_out[3:0]}), .clk(clock), .clr(reset));  // open: en
  LED led_6 (.in(signal_out[0]));
  LED led_7 (.in(signal_out[1]));
  LED led_8 (.in(signal_out[2]));
  Multiplexer #(.width(8), .enable("false")) multiplexer_2 (
    .in0({4'b0000, signal_out[3:0]}), .in1(in_5), .out(BUS_OUT), .sel(ir_out));

  assign signal_out[7:4] = control;
endmodule

module ALU (
  input  alu_out,
  input  add_sub,
  input  [7:0] a_in,
  input  [7:0] b_in,
  input  xor_not,
  input  alu_0,
  input  alu_1,
  input  [7:0] in_8,
  output [7:0] bus_out,
  output [7:0] signal_out,
  output overflow
);

  wire adder_1_cout, or_1_out, or_2_out, or_3_out, or_4_out, or_5_out, or_6_out, or_7_out, or_8_out;
  wire [3:0] xor_1_out, xor_5_out;
  wire [7:0] ADD_SUB_OUT, AND_OUT, OR_OUT, XOR_NOT_OUT;

  xor xor_1 (xor_1_out[0], b_in[0], add_sub);
  xor xor_2 (xor_1_out[1], b_in[1], add_sub);
  xor xor_3 (xor_1_out[2], b_in[2], add_sub);
  xor xor_4 (xor_1_out[3], b_in[3], add_sub);
  xor xor_5 (xor_5_out[0], b_in[4], add_sub);
  xor xor_6 (xor_5_out[1], b_in[5], add_sub);
  xor xor_7 (xor_5_out[2], b_in[6], add_sub);
  xor xor_8 (xor_5_out[3], b_in[7], add_sub);
  Adder #(.width(4)) adder_1 (.a(a_in[3:0]), .b(xor_1_out), .out(ADD_SUB_OUT[3:0]), .cin(add_sub), .cout(adder_1_cout));
  Adder #(.width(4)) adder_2 (
    .a(a_in[7:4]), .b(xor_5_out), .out(ADD_SUB_OUT[7:4]), .cin(adder_1_cout), .cout(overflow));
  or or_1 (or_1_out, xor_not, b_in[0]);
  or or_2 (or_2_out, xor_not, b_in[1]);
  or or_3 (or_3_out, xor_not, b_in[2]);
  or or_4 (or_4_out, xor_not, b_in[3]);
  or or_5 (or_5_out, xor_not, b_in[4]);
  or or_6 (or_6_out, xor_not, b_in[5]);
  or or_7 (or_7_out, xor_not, b_in[6]);
  or or_8 (or_8_out, xor_not, b_in[7]);
  xor xor_9 (XOR_NOT_OUT[0], a_in[0], or_1_out);
  xor xor_10 (XOR_NOT_OUT[1], a_in[1], or_2_out);
  xor xor_11 (XOR_NOT_OUT[2], a_in[2], or_3_out);
  xor xor_12 (XOR_NOT_OUT[3], a_in[3], or_4_out);
  xor xor_13 (XOR_NOT_OUT[4], a_in[4], or_5_out);
  xor xor_14 (XOR_NOT_OUT[5], a_in[5], or_6_out);
  xor xor_15 (XOR_NOT_OUT[6], a_in[6], or_7_out);
  xor xor_16 (XOR_NOT_OUT[7], a_in[7], or_8_out);
  and and_1 (AND_OUT[0], a_in[0], b_in[0]);
  and and_2 (AND_OUT[1], a_in[1], b_in[1]);
  and and_3 (AND_OUT[2], a_in[2], b_in[2]);
  and and_4 (AND_OUT[3], a_in[3], b_in[3]);
  and and_5 (AND_OUT[4], a_in[4], b_in[4]);
  and and_6 (AND_OUT[5], a_in[5], b_in[5]);
  and and_7 (AND_OUT[6], a_in[6], b_in[6]);
  and and_8 (AND_OUT[7], a_in[7], b_in[7]);
  Multiplexer #(.select(2), .width(8), .enable("false")) multiplexer_1 (
    .in0(ADD_SUB_OUT), .in1(AND_OUT), .in2(OR_OUT), .in3(XOR_NOT_OUT), .out(signal_out), .sel({alu_1, alu_0}));
  Multiplexer #(.width(8), .enable("false")) multiplexer_2 (.in0(signal_out), .in1(in_8), .out(bus_out), .sel(alu_out));
  or or_9 (OR_OUT[0], a_in[0], b_in[0]);
  or or_10 (OR_OUT[1], a_in[1], b_in[1]);
  or or_11 (OR_OUT[2], a_in[2], b_in[2]);
  or or_12 (OR_OUT[3], a_in[3], b_in[3]);
  or or_13 (OR_OUT[4], a_in[4], b_in[4]);
  or or_14 (OR_OUT[5], a_in[5], b_in[5]);
  or or_15 (OR_OUT[6], a_in[6], b_in[6]);
  or or_16 (OR_OUT[7], a_in[7], b_in[7]);
endmodule

module MAR (
  input  clock,
  input  mar_in,
  input  run,
  input  reset,
  input  [7:0] BUS_IN,
  input  [3:0] dips,
  output [3:0] ram
);

  wire [7:0] multiplexer_1_out, register_1_q;

  Multiplexer #(.width(8), .enable("false")) multiplexer_1 (
    .in0(BUS_IN), .in1(register_1_q), .out(multiplexer_1_out), .sel(mar_in));
  Register register_1 (.D(multiplexer_1_out), .Q(register_1_q), .clk(clock), .clr(reset));  // open: en
  LED led_1 (.in(ram[3]));
  LED led_2 (.in(ram[2]));
  LED led_3 (.in(ram[1]));
  LED led_4 (.in(ram[0]));
  Multiplexer #(.width(4), .enable("false")) multiplexer_2 (.in0(dips), .in1(register_1_q[3:0]), .out(ram), .sel(run));
endmodule

module OR (
  input  clock,
  input  [7:0] bus_in,
  input  opr_in,
  input  reset,
  output [7:0] signal_out
);

  wire [7:0] multiplexer_1_out;

  Multiplexer #(.width(8), .enable("false")) multiplexer_1 (
    .in0(bus_in), .in1(signal_out), .out(multiplexer_1_out), .sel(opr_in));
  Register register_1 (.D(multiplexer_1_out), .Q(signal_out), .clk(clock), .clr(reset));  // open: en
  LED led_1 (.in(signal_out[7]));
  LED led_2 (.in(signal_out[6]));
  LED led_3 (.in(signal_out[5]));
  LED led_4 (.in(signal_out[4]));
  LED led_5 (.in(signal_out[3]));
  LED led_6 (.in(signal_out[2]));
  LED led_7 (.in(signal_out[1]));
  LED led_8 (.in(signal_out[0]));
endmodule

module RESET (
  input  bt_reset,
  input  ncycle_end,
  output nreset,
  output reset,
  output ncycle_rst
);

  wire nand_3_out;

  nand nand_1 (nreset, bt_reset, bt_reset);
  nand nand_2 (reset, nreset, nreset);
  nand nand_3 (nand_3_out, nreset, ncycle_end);
  and and_1 (ncycle_rst, nand_3_out, nand_3_out);
endmodule

module BCD (
  input  d3,
  input  d2,
  input  d1,
  input  d0,
  output s0,
  output s1,
  output s2,
  output s3
);

  wire and_1_out, and_2_out, or_1_out;
  wire [3:0] adder_1_out;

  and and_1 (and_1_out, d2, d0);
  and and_2 (and_2_out, d2, d1);
  Adder #(.width(4)) adder_1 (.a({d3, d2, d1, d0}), .b(4'b0011), .out(adder_1_out));  // open: cin, cout
  or or_1 (or_1_out, d3, and_1_out, and_2_out);
  Multiplexer #(.width(4), .enable("false")) multiplexer_1 (
    .in0({d3, d2, d1, d0}), .in1(adder_1_out), .out({s3, s2, s1, s0}), .sel(or_1_out));
endmodule

module DISPLAY (
  input  signal,
  input  LT,
  input  BL,
  input  LE,
  input  [7:0] \input ,
  output [6:0] units,
  output [6:0] tens,
  output [6:0] hunds
);

  wire bcd_1_s0, bcd_1_s1, bcd_1_s2, bcd_2_s0, bcd_2_s1, bcd_2_s2, bcd_2_s3, bcd_3_s0, bcd_3_s1, bcd_3_s2,
       bcd_3_s3, bcd_4_s0, bcd_4_s1, bcd_4_s2, bcd_4_s3, bcd_6_s0, bcd_6_s1, bcd_6_s2, bcd_6_s3, c0, c1, d0,
       d1, d2, d3, u1, u2, u3;
  wire [7:0] BITS, negator_1_out;

  Negator negator_1 (.in(\input ), .out(negator_1_out));
  BCD bcd_1 (
    .s0(bcd_1_s0), .s1(bcd_1_s1), .s2(bcd_1_s2), .s3(c1), .d3(1'b0), .d2(bcd_2_s3), .d1(bcd_3_s3),
    .d0(bcd_4_s3));
  BCD bcd_2 (
    .s0(bcd_2_s0), .s1(bcd_2_s1), .s2(bcd_2_s2), .s3(bcd_2_s3), .d3(1'b0), .d2(BITS[7]), .d1(BITS[6]),
    .d0(BITS[5]));
  BCD bcd_3 (
    .s0(bcd_3_s0), .s1(bcd_3_s1), .s2(bcd_3_s2), .s3(bcd_3_s3), .d3(bcd_2_s2), .d2(bcd_2_s1), .d1(bcd_2_s0),
    .d0(BITS[4]));
  BCD bcd_4 (
    .s0(bcd_4_s0), .s1(bcd_4_s1), .s2(bcd_4_s2), .s3(bcd_4_s3), .d3(bcd_3_s2), .d2(bcd_3_s1), .d1(bcd_3_s0),
    .d0(BITS[3]));
  BCD bcd_5 (.s0(d1), .s1(d2), .s2(d3), .s3(c0), .d3(bcd_1_s2), .d2(bcd_1_s1), .d1(bcd_1_s0), .d0(bcd_6_s3));
  Multiplexer #(.width(8), .enable("false")) multiplexer_1 (
    .in0(\input ), .in1(negator_1_out), .out(BITS), .sel(signal));
  BCD bcd_6 (
    .s0(bcd_6_s0), .s1(bcd_6_s1), .s2(bcd_6_s2), .s3(bcd_6_s3), .d3(bcd_4_s2), .d2(bcd_4_s1), .d1(bcd_4_s0),
    .d0(BITS[2]));
  BCD bcd_7 (.s0(u1), .s1(u2), .s2(u3), .s3(d0), .d3(bcd_6_s2), .d2(bcd_6_s1), .d1(bcd_6_s0), .d0(BITS[1]));
  // DIP_744511 dip_744511_1: pin names not known; wires that end beside it: c1, 1'b0, LT, BL, LE, 1'b0, c0
  // DIP_744511 dip_744511_2: pin names not known; wires that end beside it: d1, d2, LT, BL, LE, d3, d0
  // DIP_744511 dip_744511_3: pin names not known; wires that end beside it: u1, u2, LT, BL, LE, u3, BITS[0]

  // Other names for the same wires on the sheet: u0 = BITS[0]
endmodule

module CONTROL (
  input  i3,
  input  i2,
  input  i1,
  input  i0,
  input  c2,
  input  c1,
  input  c0,
  output HLT,
  output PCI,
  output JMP,
  output PCO,
  output MAI,
  output RMI,
  output RMO,
  output IRI,
  output IRO,
  output ACO,
  output ACI,
  output SUB,
  output AL1,
  output AL0,
  output ALU,
  output NOT,
  output BRI,
  output ORI
);

  wire and_5_out, and_6_out, and_7_out, and_8_out, and_10_out, and_11_out, and_12_out, and_13_out,
       and_15_out, and_16_out, and_17_out, and_18_out, and_19_out, and_20_out, and_21_out, and_22_out,
       and_23_out, and_24_out, and_25_out, and_27_out, and_28_out, and_29_out, and_30_out, and_31_out,
       and_32_out, and_33_out, and_34_out, and_35_out, and_37_out, and_38_out, not_1_out, not_2_out,
       not_3_out, not_4_out, not_5_out, not_6_out, not_7_out;

  not not_1 (not_1_out, i3);
  not not_2 (not_2_out, i2);
  not not_3 (not_3_out, i1);
  not not_4 (not_4_out, i0);
  not not_5 (not_5_out, c2);
  not not_6 (not_6_out, c1);
  not not_7 (not_7_out, c0);
  and and_1 (HLT, c1, i3, i1, i0);
  and and_2 (PCI, not_6_out, c0);
  and and_3 (JMP, c1, not_7_out, i3, not_2_out, i1);
  and and_4 (PCO, not_5_out, not_6_out, not_7_out);
  and and_5 (and_5_out, c1, not_7_out, i3, not_3_out, not_4_out);
  and and_6 (and_6_out, c1, not_7_out, not_1_out, i2);
  and and_7 (and_7_out, c1, not_7_out, not_1_out, i0);
  and and_8 (and_8_out, not_5_out, not_6_out, not_7_out);
  and and_9 (RMI, c1, c0, not_2_out, i1, i0);
  and and_10 (and_10_out, c0, i3, not_3_out, not_4_out);
  and and_11 (and_11_out, c0, not_1_out, i2);
  and and_12 (and_12_out, c0, not_1_out, not_3_out, i0);
  and and_13 (and_13_out, not_6_out, c0);
  and and_14 (IRI, not_6_out, c0);
  and and_15 (and_15_out, c1, not_7_out, i3, not_2_out, not_4_out);
  and and_16 (and_16_out, c1, not_7_out, not_1_out, i2);
  and and_17 (and_17_out, c1, not_7_out, not_1_out, i0);
  and and_18 (and_18_out, c1, not_7_out, not_2_out, i1);
  and and_19 (and_19_out, c1, c0, not_2_out, i1, i0);
  and and_20 (and_20_out, c1, not_7_out, i3, i2, not_4_out);
  and and_21 (and_21_out, c2, i3, not_3_out, not_4_out);
  and and_22 (and_22_out, c2, not_1_out, i2);
  and and_23 (and_23_out, c1, c0, not_1_out, not_2_out, not_3_out, i0);
  and and_24 (and_24_out, c1, not_7_out, i3, not_3_out, i0);
  and and_25 (and_25_out, c1, not_7_out, not_1_out, not_2_out, i1, not_4_out);
  and and_26 (SUB, c2, i2, not_3_out, i0);
  and and_27 (and_27_out, c2, i3, not_3_out, not_4_out);
  and and_28 (and_28_out, c2, i2, i1, i0);
  and and_29 (and_29_out, c1, not_7_out, i3, not_3_out, i0);
  and and_30 (and_30_out, c2, i3, not_3_out, not_4_out);
  and and_31 (and_31_out, c2, not_1_out, i2, i1, not_4_out);
  and and_32 (and_32_out, c1, not_7_out, i3, not_3_out, i0);
  and and_33 (and_33_out, c2, i3, not_3_out, not_4_out);
  and and_34 (and_34_out, c2, not_1_out, i2);
  and and_35 (and_35_out, c1, not_7_out, i3, not_3_out, i0);
  and and_36 (NOT, c1, not_7_out, i3, not_3_out, i0);
  and and_37 (and_37_out, c1, c0, i3, not_3_out, not_4_out);
  and and_38 (and_38_out, c1, c0, not_1_out, i2);
  and and_39 (ORI, c1, not_7_out, i3, i2, not_4_out);
  or or_1 (RMO, and_10_out, and_11_out, and_12_out, and_13_out);
  or or_2 (IRO, and_15_out, and_16_out, and_17_out, and_18_out);
  or or_3 (ACO, and_19_out, and_20_out);
  or or_4 (ACI, and_21_out, and_22_out, and_23_out, and_24_out, and_25_out);
  or or_5 (BRI, and_37_out, and_38_out);
  or or_6 (MAI, and_5_out, and_6_out, and_7_out, and_8_out);
  or or_7 (AL1, and_27_out, and_28_out, and_29_out);
  or or_8 (AL0, and_30_out, and_31_out, and_32_out);
  or or_9 (ALU, and_33_out, and_34_out, and_35_out);
endmodule

module COUNTER (
  input  nclock,
  input  ncycle_rst,
  output ncycle_end,
  output [4:0] status,
  output [2:0] couter_out
);

  wire [4:0] undriven;

  Counter #(.width(3), .max('h7)) counter_1 (
    .load(1'b0), .count(1'b1), .Q(couter_out), .clk(nclock), .clr(ncycle_rst));  // open: D, carry
  // DIP_74138 dip_74138_1: pin names not known; wires that end beside it: couter_out[0], couter_out[1], couter_out[2], 1'b0, 1'b0, 1'b1, ncycle_end
  // Probe on undriven
  assign status = ~undriven;  // NOT_Gate not_1, 5 bits wide

  // Other names for the same wires on the sheet: COUNTER_OUT[2:0] = couter_out
endmodule
